# Fritzing sketch PIRRelayUno5V (saved by Fritzing 0.9.2b)

parts:
  Part3 = Arduino Uno (Rev3) - ICSP
  U1 = RELAY [package=relay-jzc]
  BC338 = TRANSISTOR_NPN_2 [package=to-92]
  R1 = Resistor [tolerance=±5% resistance=1k package="1206 [SMD]"]
  D3 = Rectifier Diode [part_number=Rectifier package="Melf DO-213 AA [SMD]"]
  5V = Power plug
  R5 = Resistor [tolerance=±5% resistance=10k package="1206 [SMD]"]
  PIR1 = PIR sensor

nets:
  GND: Part3.GND, BC338.E, 5V.GND, PIR1.GND
  N1: Part3.D4, R1.Pin_1
  N2: Part3.D7, R5.Pin_1, PIR1.SIG
  VCC: Part3.5V, U1.COIL2, D3.cathode, 5V.VCC, R5.Pin_0, PIR1.VCC
  N3: U1.COIL1, BC338.C, D3.anode
  N4: BC338.B, R1.Pin_0
